# Fritzing sketch Sketch (saved by Fritzing 0.9.3b)
breadboards: 1

parts:
  U1 = NodeMCU V3.0
  YL-83_-_Detection_Board1 = YL-83 Rain Sensor - Detection Board
  YL-83_-_Control_Board1 = YL-83 Rain Sensor - Control Board
  YwRobot_Power_Supply1 = YwRobot Breadboard Power Supply [part_number=545043]
  R1 = Resistor [tolerance=±5% resistance=220 package="0805 [SMD]"]
  LED1 = LEDs [package=led10mm]

nets:
  N1: U1.D0, YL-83_-_Control_Board1.DO
  N2: U1.D1, R1.Pin_0
  GND: U1.GND, YL-83_-_Control_Board1.GND, YwRobot_Power_Supply1.GND#13, YwRobot_Power_Supply1.GND#14, LED1.A
  VIN: U1.Vin, YL-83_-_Control_Board1.VCC, YwRobot_Power_Supply1.VCC#9, YwRobot_Power_Supply1.VCC#10
  N3: U1.A0, YL-83_-_Control_Board1.AO
  N4: YL-83_-_Detection_Board1.POS, YL-83_-_Control_Board1.POS
  N5: YL-83_-_Detection_Board1.NEG, YL-83_-_Control_Board1.NEG
  N6: YwRobot_Power_Supply1.VCC#5, YwRobot_Power_Supply1.VCC#6
  N7: YwRobot_Power_Supply1.GND#11, YwRobot_Power_Supply1.GND#12
  N8: R1.Pin_1, LED1.C

custom parts:
  NodeMCU V3.0: ESP8266 based NodeMCU
  YL-83 Rain Sensor - Detection Board: The YL-83 is a rain sensor that has more resistance when dry and less resistance when wet. The module runs at 5V.
  YL-83 Rain Sensor - Control Board: The YL-83 is a rain sensor that has more resistance when dry and less resistance when wet. The module runs at 5V.
  YwRobot Breadboard Power Supply: The YwRobot Breadboard Power Supply (MB-V2) has two power rails; they can be 5V or 3V3. Power to the module can be provided through the female USB socket or through the A10 (female) 2.1mm power jack.
